# Fritzing sketch 8-bit computer fritzing (saved by Fritzing 0.9.6b)
breadboards: 17

parts:
  SW1 = DIP SWITCH [package=dipswitch-02]
  SW2 = DIP SWITCH [package=dipswitch-02]
  SW3 = DIP Switch 8 Position [package=dipswitch-08]  # not connected
  S1 = Pushbutton [package="[THT]"]
  IC5 = IC, DIP package, 20 pins [chip_label=SN74LS273N]  # not connected
  IC6 = IC, DIP package, 16 pins [chip_label=SN74LS157N]
  IC7 = IC, DIP package, 16 pins [chip_label=SN74LS157N]  # not connected
  IC8 = IC, DIP package, 16 pins [chip_label=SN74LS157N]  # not connected
  IC9 = IC, DIP package, 16 pins [chip_label=SN74LS157N]
  S2 = Pushbutton [package="[THT]"]
  S3 = Pushbutton [package="[THT]"]  # not connected
  IC10 = IC, DIP package, 8 pins [chip_label=555]
  IC11 = IC, DIP package, 8 pins [chip_label=555]  # not connected
  IC12 = IC, DIP package, 8 pins [chip_label=555]  # not connected
  IC13 = IC, DIP package, 14 pins [chip_label=74LS08]  # not connected
  IC14 = IC, DIP package, 14 pins [chip_label=74LS04]  # not connected
  IC15 = IC, DIP package, 14 pins [chip_label=74LS32]
  LED1 = smd LED [color="Red (633nm)" package="1206 [SMD]"]  # not connected
  LED2 = smd LED [color="Red (633nm)" package="1206 [SMD]"]  # not connected
  LED3 = smd LED [color="Red (633nm)" package="1206 [SMD]"]  # not connected
  LED4 = smd LED [color="Red (633nm)" package="1206 [SMD]"]  # not connected
  LED5 = smd LED [color="Red (633nm)" package="1206 [SMD]"]  # not connected
  LED6 = smd LED [color="Red (633nm)" package="1206 [SMD]"]  # not connected
  LED7 = smd LED [color="Red (633nm)" package="1206 [SMD]"]  # not connected
  LED8 = smd LED [color="Red (633nm)" package="1206 [SMD]"]  # not connected
  LED9 = smd LED [color="Red (633nm)" package="1206 [SMD]"]  # not connected
  LED10 = smd LED [color="Red (633nm)" package="1206 [SMD]"]  # not connected
  LED11 = smd LED [color="Red (633nm)" package="1206 [SMD]"]  # not connected
  LED12 = smd LED [color="Red (633nm)" package="1206 [SMD]"]  # not connected
  LED13 = smd LED [color="Red (633nm)" package="1206 [SMD]"]  # not connected
  LED14 = smd LED [color="Red (633nm)" package="1206 [SMD]"]  # not connected
  LED15 = smd LED [color="Red (633nm)" package="1206 [SMD]"]  # not connected
  IC16 = IC, DIP package, 24 pins [chip_label=EEPROM]  # not connected
  IC17 = IC, DIP package, 24 pins [chip_label=EEPROM]  # not connected
  IC18 = IC, DIP package, 24 pins [chip_label=EEPROM]  # not connected
  DI1 = 7-Segment LED Display [package=THT]  # not connected
  DI2 = 7-Segment LED Display [package=THT]  # not connected
  DI3 = 7-Segment LED Display [package=THT]  # not connected
  DI4 = 7-Segment LED Display [package=THT]  # not connected
  Part1 = Arduino Mega 2560 (Rev3)
  LED16 = smd LED [color="Red (633nm)" package="1206 [SMD]"]  # not connected
  LED17 = smd LED [color="Red (633nm)" package="1206 [SMD]"]  # not connected
  LED21 = smd LED [color="Red (633nm)" package="1206 [SMD]"]  # not connected
  Part2 = Arduino Nano (Rev3.0)
  S4 = Pushbutton [package="[THT]"]
  R1 = Resistor [tolerance=±5% resistance=1k package="0603 [SMD]"]
  D1 = LED_BARGRAPH_10 [package=led_bargaph_10]
  IC20 = IC, DIP package, 16 pins [chip_label=74189]  # not connected
  IC21 = IC, DIP package, 16 pins [chip_label=SN74LS157N]  # not connected
  IC22 = IC, DIP package, 16 pins  # not connected
  IC23 = IC, DIP package, 16 pins  # not connected
  IC24 = IC, DIP package, 20 pins [chip_label=74LS245]  # not connected
  IC25 = IC, DIP package, 14 pins  # not connected
  IC26 = IC, DIP package, 20 pins  # not connected
  IC27 = IC, DIP package, 14 pins [chip_label=SN74LS173AN]  # not connected
  IC28 = IC, DIP package, 14 pins [chip_label=SN74LS173AN]  # not connected
  D2 = LED_BARGRAPH_10 [package=led_bargaph_10]  # not connected
  D3 = LED_BARGRAPH_10 [package=led_bargaph_10]  # not connected
  IC29 = IC, DIP package, 16 pins  # not connected
  IC30 = IC, DIP package, 16 pins  # not connected
  IC31 = IC, DIP package, 14 pins [chip_label=SN74LS00N]  # not connected
  IC32 = IC, DIP package, 20 pins [chip_label=74LS245]  # not connected
  IC33 = IC, DIP package, 16 pins  # not connected
  LED22 = smd LED [color="Red (633nm)" package="1206 [SMD]"]  # not connected
  LED23 = smd LED [color="Red (633nm)" package="1206 [SMD]"]  # not connected
  LED24 = smd LED [color="Red (633nm)" package="1206 [SMD]"]  # not connected
  LED25 = smd LED [color="Red (633nm)" package="1206 [SMD]"]  # not connected
  IC34 = IC, DIP package, 20 pins [chip_label=74LS245]  # not connected
  D4 = LED_BARGRAPH_10 [package=led_bargaph_10]  # not connected
  IC19 = IC, DIP package, 16 pins [chip_label=SN74LS173AN]  # not connected
  IC37 = IC, DIP package, 16 pins [chip_label=SN74LS173AN]  # not connected
  IC38 = IC, DIP package, 16 pins [chip_label=SN74LS173AN]  # not connected
  IC39 = IC, DIP package, 20 pins [chip_label=74LS245]  # not connected
  IC40 = IC, DIP package, 16 pins  # not connected
  IC41 = IC, DIP package, 16 pins  # not connected
  IC42 = IC, DIP package, 14 pins  # not connected
  IC43 = IC, DIP package, 14 pins  # not connected
  D5 = LED_BARGRAPH_10 [package=led_bargaph_10]  # not connected
  D6 = LED_BARGRAPH_10 [package=led_bargaph_10]  # not connected
  IC44 = IC, DIP package, 16 pins [chip_label=SN74LS173AN]  # not connected
  IC45 = IC, DIP package, 16 pins [chip_label=SN74LS173AN]  # not connected
  IC46 = IC, DIP package, 20 pins [chip_label=74LS245]  # not connected
  IC47 = IC, DIP package, 8 pins [chip_label=555]  # not connected
  IC48 = IC, DIP package, 14 pins [chip_label=DM74LS107AN]  # not connected
  IC49 = IC, DIP package, 16 pins [chip_label=GD74LS139]  # not connected
  IC50 = IC, DIP package, 14 pins [chip_label=DM74LS107AN]
  IC51 = IC, DIP package, 14 pins  # not connected
  IC52 = IC, DIP package, 14 pins  # not connected
  D7 = LED_BARGRAPH_10 [package=led_bargaph_10]  # not connected
  LED26 = smd LED [color="Red (633nm)" package="1206 [SMD]"]
  LED27 = smd LED [color="Red (633nm)" package="1206 [SMD]"]
  LED28 = smd LED [color="Red (633nm)" package="1206 [SMD]"]
  LED29 = smd LED [color="Red (633nm)" package="1206 [SMD]"]
  LED30 = smd LED [color="Red (633nm)" package="1206 [SMD]"]
  U1 = POT [package=3362u]

nets:
  N1: SW1.1, SW1.2
  N2: SW1.3, IC9.pin2
  N3: SW1.4, IC9.pin5
  N4: SW2.1, IC9.pin11
  N5: SW2.2, IC9.pin14
  N6: SW2.3, SW2.4
  N7: S1.Pin_1, S1.Pin_2, IC6.pin14
  N8: S1.Pin_3, S1.Pin_4
  N9: S2.Pin_1, S2.Pin_2
  N10: S2.Pin_3, S2.Pin_4
  N11: IC10.pin5, U1.E
  N12: IC15.pin14, LED30.anode
  N13: Part1.SCL, Part2.A5
  N14: Part1.SDA, Part2.A4
  N15: Part1.D3_PWM, S4.Pin_3, S4.Pin_4
  N16: Part1.GND, R1.Pin_1
  N17: Part2.D2, IC50.pin13
  N18: S4.Pin_1, S4.Pin_2, R1.Pin_0
  N19: D1.A_C, LED29.anode
  N20: LED26.cathode, LED27.cathode, LED28.cathode, LED29.cathode

notes:
  Button:
  In Manual Clock
  Button:
  In Program Mode
  Dipswitch:
  All ON (up)
  Yellow:
  Program Button
  Blue:
  Memory
  Addr
  Dipswitch
  Green:
  Memory Value Dipswitch
  Yellow:
  Output
  Blue:
  Bus
  White:
  Control Bits
  #define PIN_BUS1 23 //PIN1 (far left) of Bus
  #define PIN_BUS2 25
  #define PIN_BUS3 27
  #define PIN_BUS4 29
  #define PIN_BUS5 31
  #define PIN_BUS6 33
  #define PIN_BUS7 35
  #define PIN_BUS8 37
  #define PIN_CONTROL_HALT 52 //Halt clock
  #define PIN_CONTROL_MEMORY_ADDRESS_IN 24 //Memory address register IN
  #define PIN_CONTROL_RAM_IN 26 //RAM data IN
  #define PIN_CONTROL_RAM_OUT 28 //RAM data OUT
  #define PIN_CONTROL_INSTRUCTION_OUT 30 //Instruction register OUT
  #define PIN_CONTROL_INSTRUCTION_IN 32 //Instruction register IN
  #define PIN_CONTROL_A_REGISTER_IN 34 //A register IN
  #define PIN_CONTROL_A_REGISTER_OUT 36 //A register out
  #define PIN_CONTROL_SUM_OUT 38 //ALU OUT
  #define PIN_CONTROL_SUBTRACT 40 //ALU Subtract
  #define PIN_CONTROL_B_INSTRUCTION_IN 42 //B register IN
  #define PIN_CONTROL_OUTPUT_IN 39 //Output register IN
  #define PIN_CONTROL_COUNTER_ENABLE 41 //Program counter ENABLE
  #define PIN_CONTROL_COUNTER_OUT 43 //Program counter OUT
  #define PIN_CONTROL_JUMP 45 //Jump
  #define PIN_CONTROL_FLAGS 22 //Flags
  #define PIN_LED_OUT_128 A7 //Value 128 for output LED segment display
  #define PIN_LED_OUT_64 A6 //Value 64 for output LED segment display
  #define PIN_LED_OUT_32 A5 //Value 32 for output LED segment display
  #define PIN_LED_OUT_16 A4 //Value 16 for output LED segment display
  #define PIN_LED_OUT_8 A3 //Value 8 for output LED segment display
  #define PIN_LED_OUT_4 A2 //Value 4 for output LED segment display
  #define PIN_LED_OUT_2 A1 //Value 2 for output LED segment display
  #define PIN_LED_OUT_1 A0 //Value 1 for output LED segment display
  #define PIN_SET_RAM A15 //Program RAM button
  #define PIN_RAM_128 44 //Pins for setting bits for writing to RAM
  #define PIN_RAM_64 46
  #define PIN_RAM_32 48
  #define PIN_RAM_16 50
  #define PIN_RAM_8 10
  #define PIN_RAM_4 11
  #define PIN_RAM_2 12
  #define PIN_RAM_1 13
  #define PIN_RAM_ADDR_8 47 //Pins for setting address of RAM
  #define PIN_RAM_ADDR_4 49
  #define PIN_RAM_ADDR_2 51
  #define PIN_RAM_ADDR_1 53
  #define PIN_CLOCK 2 //Pin for clock from 555 IC
  #define PIN_LOAD_DEFAULTS 3 //Pin for button interrupts to load default program
  Arduino connection wiring diagram.
  Based on Ben Eater's 8-bit computer reference design.
  White:
  Clock
